// Logisim project da1_task2.circ as structural Verilog: 2 circuits, main circuit DUT
module DUT (
  input  [6:0] SIGN,
  input  [6:0] D1,
  input  [6:0] D0,
  output [7:0] TC,
  output NAN
);

  wire nand_1_out, nand_2_out, nand_3_out, nand_4_out, nand_5_out, nand_6_out, nand_7_out, not_1_out,
       not_2_out, not_3_out, not_4_out, not_5_out, not_6_out, not_7_out, not_8_out, not_9_out, not_10_out,
       not_13_out;
  wire [4:0] bit_extender_3_out, bit_extender_4_out, nand_10_out, nand_11_out, nand_13_out;
  wire [6:0] adder_2_out, bit_extender_1_out, bit_extender_2_out, nand_8_out, nand_9_out, nand_12_out;
  wire [7:0] adder_1_out, bit_extender_5_out, multiplexer_1_out, not_11_out, not_12_out, uval;

  not not_1 (not_1_out, SIGN[6]);
  not not_2 (not_2_out, SIGN[4]);
  not not_3 (not_3_out, D0[6]);
  not not_4 (not_4_out, D0[2]);
  not not_5 (not_5_out, D0[1]);
  not not_6 (not_6_out, D1[6]);
  not not_7 (not_7_out, D1[2]);
  not not_8 (not_8_out, D1[1]);
  nand nand_1 (nand_1_out, SIGN[1], not_9_out);
  not not_9 (not_9_out, SIGN[2]);
  not not_10 (not_10_out, SIGN[1]);
  nand nand_2 (nand_2_out, not_10_out, SIGN[2]);
  nand nand_3 (nand_3_out, D0[3], nand_4_out);
  nand nand_4 (nand_4_out, not_4_out, not_5_out);
  nand nand_5 (nand_5_out, D1[3], nand_6_out);
  nand nand_6 (nand_6_out, not_7_out, not_8_out);
  assign bit_extender_1_out = {{6{D1[3]}}, D1[3]};  // Bit_Extender bit_extender_1
  assign bit_extender_2_out = {{6{D1[2]}}, D1[2]};  // Bit_Extender bit_extender_2
  assign bit_extender_3_out = {{4{D1[1]}}, D1[1]};  // Bit_Extender bit_extender_3
  assign bit_extender_4_out = {{4{D1[0]}}, D1[0]};  // Bit_Extender bit_extender_4
  nand nand_7 (nand_7_out, nand_1_out, nand_2_out);
  assign nand_8_out = ~(7'b1010000 & bit_extender_1_out);  // NAND_Gate nand_8, 7 bits wide
  assign nand_9_out = ~(7'b0101000 & bit_extender_2_out);  // NAND_Gate nand_9, 7 bits wide
  assign nand_10_out = ~(5'b10100 & bit_extender_3_out);  // NAND_Gate nand_10, 5 bits wide
  assign nand_11_out = ~(5'b01010 & bit_extender_4_out);  // NAND_Gate nand_11, 5 bits wide
  assign not_11_out = ~uval;  // NOT_Gate not_11, 8 bits wide
  Adder adder_1 (.a(not_11_out), .b(8'h1), .out(adder_1_out));  // open: cin, cout
  assign nand_12_out = ~(nand_8_out & nand_9_out);  // NAND_Gate nand_12, 7 bits wide
  Adder #(.width(7)) adder_2 (.a(nand_12_out), .b({2'b00, nand_13_out}), .out(adder_2_out));  // open: cin, cout
  assign nand_13_out = ~(nand_10_out & nand_11_out);  // NAND_Gate nand_13, 5 bits wide
  Multiplexer #(.width(8)) multiplexer_1 (.in0(uval), .in1(adder_1_out), .out(multiplexer_1_out), .sel(SIGN[2]));
  Adder #(.width(7)) adder_3 (.a(adder_2_out), .b({3'b000, D0[3:0]}), .out(uval[6:0]), .cout(uval[7]));  // open: cin
  nand nand_14 (NAN, SIGN[0], nand_7_out, SIGN[3], not_2_out, SIGN[5], not_1_out, not_3_out, D0[5], D0[4], nand_3_out, not_6_out, D1[5], D1[4], nand_5_out);
  assign not_12_out = ~multiplexer_1_out;  // NOT_Gate not_12, 8 bits wide
  assign bit_extender_5_out = {{7{not_13_out}}, not_13_out};  // Bit_Extender bit_extender_5
  not not_13 (not_13_out, NAN);
  assign TC = ~(not_12_out & bit_extender_5_out);  // NAND_Gate nand_15, 8 bits wide

  // Other names for the same wires on the sheet: d0_t[3:0] = D0[3:0]; sign_t = SIGN[2]

  // Notes on the sheet:
  //   Please put your deisgn below. You may also use subcircuits.
  //   However, do not move or rename any pins.
endmodule

module TB (
  input  [6:0] SIGN,
  input  [6:0] D1,
  input  [6:0] D0,
  output [7:0] DOUT,
  output NAN
);

  DUT dut_1 (.SIGN(SIGN), .D1(D1), .D0(D0), .TC(DOUT), .NAN(NAN));

  // Notes on the sheet:
  //   DO NOT MODIFY THIS
  //   TEST YOUR CIRCUITS USING THIS TO MAKE SURE YOU HAVE NOT ALTERED PIN OUT
endmodule
