// Logisim project da1_task3.circ as structural Verilog: 3 circuits, main circuit DUT
module DUT (
  input  X,
  input  CLK,
  input  RST,
  output Z
);

  wire adder_1_cout, nand_2_out, nand_3_out, nand_4_out, nand_5_out, nand_6_out, nand_7_out, nand_8_out,
       nand_9_out, nand_10_out, nand_11_out, nand_12_out, nand_13_out, nand_14_out, nand_15_out, nand_16_out,
       not_1_out, not_3_out, not_4_out, not_5_out, not_6_out, not_8_out, t_ff_4_qn, t_ff_5_qn;
  wire [1:0] curmod;
  wire [2:0] adder_1_out, adder_2_out, bit_extender_1_out, cursum, nand_1_out, negcursum, not_2_out, nxtsum;

  not not_1 (not_1_out, RST);
  assign bit_extender_1_out = {{2{not_1_out}}, not_1_out};  // Bit_Extender bit_extender_1
  assign nand_1_out = ~(nxtsum & bit_extender_1_out);  // NAND_Gate nand_1, 3 bits wide
  assign not_2_out = ~nand_1_out;  // NOT_Gate not_2, 3 bits wide
  not not_3 (not_3_out, not_2_out[2]);
  not not_4 (not_4_out, not_2_out[1]);
  not not_5 (not_5_out, not_2_out[0]);
  nand nand_2 (nand_2_out, not_3_out, cursum[2]);
  nand nand_3 (nand_3_out, not_2_out[2], negcursum[2]);
  nand nand_4 (nand_4_out, not_4_out, cursum[1]);
  nand nand_5 (nand_5_out, not_2_out[1], negcursum[1]);
  nand nand_6 (nand_6_out, not_5_out, cursum[0]);
  nand nand_7 (nand_7_out, nand_6_out, nand_8_out);
  nand nand_8 (nand_8_out, not_2_out[0], negcursum[0]);
  nand nand_9 (nand_9_out, negcursum[0], negcursum[1]);
  Adder #(.width(3)) adder_1 (.a(cursum), .b({1'b0, curmod}), .out(adder_1_out), .cin(1'b1), .cout(adder_1_cout));
  T_Flip_Flop t_ff_1 (.T(nand_10_out), .clk(CLK), .Q(cursum[2]), .Qn(negcursum[2]));  // open: reset, preset
  nand nand_10 (nand_10_out, nand_2_out, nand_3_out);
  T_Flip_Flop t_ff_2 (.T(nand_11_out), .clk(CLK), .Q(cursum[1]), .Qn(negcursum[1]));  // open: reset, preset
  nand nand_11 (nand_11_out, nand_4_out, nand_5_out);
  T_Flip_Flop t_ff_3 (.T(nand_7_out), .clk(CLK), .Q(cursum[0]), .Qn(negcursum[0]));  // open: reset, preset
  not not_6 (not_6_out, nand_9_out);
  nand nand_12 (nand_12_out, not_6_out, negcursum[2]);
  Adder #(.width(3)) adder_2 (.a(adder_1_out), .b(3'b000), .out(adder_2_out), .cin(adder_1_cout));  // open: cout
  not not_7 (Z, nand_12_out);
  // Probe on cursum
  // Probe on adder_2_out
  Multiplexer #(.width(3)) multiplexer_1 (.in0(cursum), .in1(adder_2_out), .out(nxtsum), .sel(X));
  nand nand_13 (nand_13_out, t_ff_4_qn, t_ff_5_qn);
  nand nand_14 (nand_14_out, curmod[0], curmod[1]);
  nand nand_15 (nand_15_out, RST, CLK);
  not not_8 (not_8_out, nand_15_out);
  T_Flip_Flop t_ff_4 (.T(curmod[0]), .clk(CLK), .Q(curmod[1]), .Qn(t_ff_4_qn), .reset(not_8_out));  // open: preset
  T_Flip_Flop t_ff_5 (.T(nand_16_out), .clk(CLK), .Q(curmod[0]), .Qn(t_ff_5_qn), .reset(not_8_out));  // open: preset
  nand nand_16 (nand_16_out, nand_13_out, nand_14_out);

  // Other names for the same wires on the sheet: o = Z

  // Notes on the sheet:
  //   Please put your deisgn below. You may also use subcircuits.
  //   However, do not move, rename, add, or delete any pins.
endmodule

module TB (
);

  wire clk_out, mypor_1_p2, not_1_out, or_1_out, RESET_out, TimeIndex_carry, undriven;
  wire [0:0] dut_1_z;
  wire [4:0] TimeIndex_q;

  Clock #(.highDuration(2), .lowDuration(2)) clk (.out(clk_out));
  Clock sysclk ();  // open: out
  Counter #(.max('h1f), .ongoal("stay"), .width(5)) TimeIndex (
    .load(or_1_out), .clk(clk_out), .D({5{1'b0}}), .carry(TimeIndex_carry), .Q(TimeIndex_q));  // open: clr, up, count
  // MyPOR mypor_1: pin names not known; wires that end beside it: clk_out, mypor_1_p2
  Button RESET (.out(RESET_out));
  ROM #(.addrWidth(5), .dataWidth(1)) TestTraceMemory (.addr(TimeIndex_q));  // open: data
  or or_1 (or_1_out, mypor_1_p2, RESET_out);
  not not_1 (not_1_out, TimeIndex_carry);
  DUT dut_1 (.X(undriven), .CLK(clk_out), .RST(or_1_out), .Z(dut_1_z[0]));
  TTY tty_1 (.data({6'b011000, dut_1_z[0]}), .clk(clk_out), .we(not_1_out), .clr(or_1_out));
  LED DONE (.in(TimeIndex_carry));

  // Notes on the sheet:
  //   DO NOT MODIFY THIS
  //   YOU MAY TEST YOUR CIRCUITS USING THIS TO MAKE SURE YOU HAVE NOT ALTERED PIN OUT
  //   Edit ROM with input trace of 32 bits
endmodule

module TBRANDOM (
);

  wire clk_out, mypor_1_p2, not_1_out, or_1_out, random_1_out, RESET_out, TimeIndex_carry;
  wire [0:0] dut_1_z;

  Clock #(.highDuration(2), .lowDuration(2)) clk (.out(clk_out));
  Clock sysclk ();  // open: out
  Counter #(.ongoal("stay")) TimeIndex (
    .load(or_1_out), .clk(clk_out), .D({8{1'b0}}), .carry(TimeIndex_carry));  // open: clr, up, count, Q
  // MyPOR mypor_1: pin names not known; wires that end beside it: clk_out, mypor_1_p2
  Button RESET (.out(RESET_out));
  or or_1 (or_1_out, mypor_1_p2, RESET_out);
  Random #(.width(1)) random_1 (.clr(or_1_out), .clk(clk_out), .out(random_1_out));  // open: next
  not not_1 (not_1_out, TimeIndex_carry);
  DUT dut_1 (.X(random_1_out), .CLK(clk_out), .RST(or_1_out), .Z(dut_1_z[0]));
  TTY tty_1 (.data({6'b011000, dut_1_z[0]}), .clk(clk_out), .we(not_1_out), .clr(or_1_out));
  LED DONE (.in(TimeIndex_carry));

  // Notes on the sheet:
  //   DO NOT MODIFY THIS
  //   YOU MAY TEST YOUR CIRCUITS USING THIS TO MAKE SURE YOU HAVE NOT ALTERED PIN OUT
endmodule
