// Logisim project da1_task4.circ as structural Verilog: 2 circuits, main circuit DUT
module DUT (
  input  [15:0] DIN1,
  input  [15:0] DIN2,
  input  [15:0] DIN3,
  input  GO1,
  input  GO2,
  input  GO3,
  input  CLK,
  input  RST,
  output [15:0] DOUT,
  output DONE
);

  wire d_ff_1_q, d_ff_2_q, d_ff_3_q, nand_2_out, nand_3_out, nand_4_out, nand_5_out, nand_7_out, nand_8_out,
       nand_9_out, nand_10_out, nand_12_out, nand_13_out, nand_14_out, nand_15_out, not_1_out, not_2_out,
       not_4_out, not_6_out, not_7_out, V1;
  wire [15:0] bit_extender_1_out, D1, nand_1_out, nand_6_out, nand_11_out, not_3_out, not_5_out, not_8_out,
       undriven;

  Register #(.width(17)) register_1 (.D({undriven, 1'b1}), .Q({D1, V1}));  // open: en, clk, clr
  assign bit_extender_1_out = {{15{not_1_out}}, not_1_out};  // Bit_Extender bit_extender_1
  not not_1 (not_1_out, RST);
  not not_2 (not_2_out, RST);
  assign nand_1_out = ~(DIN1 & bit_extender_1_out);  // NAND_Gate nand_1, 16 bits wide
  assign not_3_out = ~nand_1_out;  // NOT_Gate not_3, 16 bits wide
  not not_4 (not_4_out, GO1);
  nand nand_2 (nand_2_out, not_4_out, not_1_out);
  nand nand_3 (nand_3_out, d_ff_1_q, not_2_out);
  nand nand_4 (nand_4_out, nand_3_out, nand_5_out);
  nand nand_5 (nand_5_out, not_2_out, GO1);
  Register #(.width(16)) register_2 (.D(not_3_out), .en(nand_2_out), .clk(CLK));  // open: Q, clr
  D_Flip_Flop d_ff_1 (.D(nand_4_out), .clk(CLK), .Q(d_ff_1_q));  // open: Qn, preset, reset
  Register #(.width(16)) register_3 (.D(not_5_out), .en(nand_7_out), .clk(CLK));  // open: Q, clr
  assign nand_6_out = ~(DIN2 & bit_extender_1_out);  // NAND_Gate nand_6, 16 bits wide
  assign not_5_out = ~nand_6_out;  // NOT_Gate not_5, 16 bits wide
  not not_6 (not_6_out, GO2);
  nand nand_7 (nand_7_out, not_6_out, not_1_out);
  D_Flip_Flop d_ff_2 (.D(nand_9_out), .clk(CLK), .Q(d_ff_2_q));  // open: Qn, preset, reset
  nand nand_8 (nand_8_out, d_ff_2_q, not_2_out);
  nand nand_9 (nand_9_out, nand_8_out, nand_10_out);
  nand nand_10 (nand_10_out, not_2_out, GO2);
  assign nand_11_out = ~(DIN3 & bit_extender_1_out);  // NAND_Gate nand_11, 16 bits wide
  not not_7 (not_7_out, GO3);
  nand nand_12 (nand_12_out, d_ff_3_q, not_2_out);
  nand nand_13 (nand_13_out, not_2_out, GO3);
  Register #(.width(16)) register_4 (.D(not_8_out), .en(nand_14_out), .clk(CLK));  // open: Q, clr
  assign not_8_out = ~nand_11_out;  // NOT_Gate not_8, 16 bits wide
  nand nand_14 (nand_14_out, not_7_out, not_1_out);
  D_Flip_Flop d_ff_3 (.D(nand_15_out), .clk(CLK), .Q(d_ff_3_q));  // open: Qn, preset, reset
  nand nand_15 (nand_15_out, nand_12_out, nand_13_out);

  // Notes on the sheet:
  //   Please put your design below. You may also use subcircuits.
  //   However, do not move, rename, add, or delete any pins.
endmodule

module TB (
  input  [15:0] DIN1,
  input  [15:0] DIN2,
  input  [15:0] DIN3,
  input  GO1,
  input  GO2,
  input  GO3,
  input  RST,
  output [15:0] DOUT,
  output DONE
);

  wire clk_out, or_1_out, RESET_out;

  Clock sysclk ();  // open: out
  Button RESET (.out(RESET_out));
  Clock #(.highDuration(2), .lowDuration(2)) clk (.out(clk_out));
  or or_1 (or_1_out, RESET_out, RST);
  DUT dut_1 (
    .DIN1(DIN1), .DIN2(DIN2), .DIN3(DIN3), .GO1(GO1), .GO2(GO2), .GO3(GO3), .CLK(clk_out), .RST(or_1_out),
    .DOUT(DOUT), .DONE(DONE));

  // Notes on the sheet:
  //   DO NOT MODIFY THIS
  //   YOU MAY TEST YOUR CIRCUITS USING THIS TO MAKE SURE YOU HAVE NOT ALTERED PIN OUT
endmodule
